# Fritzing sketch particle-squared (saved by Fritzing 0.9.3b)

parts:
  Part1 = Adafruit Si7021 Temp Humidity [part_number="Adafruit #3251"]
  Part3 = Adafruit CCS811
  Part4 = Adafruit Feather nRF52840 [part_number=4062]

nets:
  N1: Part1.SDA, Part3.SDA, Part4.SDA
  N2: Part1.SCL, Part3.SCL, Part4.SCL
  GND: Part1.GND, Part3.GND, Part4.GND
  VIN: Part1.VIN, Part3.VIN, Part4.VBUS
  N3: Part3.!WAKE, Part4.D11
  N4: Part3.!RESET, Part4.D12
  N5: Part3.!INT, Part4.D13

notes:
  To HPMA1150

custom parts:
  Adafruit Si7021 Temp Humidity: It's summer and you're sweating and your hair's all frizzy and all you really want to know is why the weatherman said this morning that today's relative humidity would max out at a perfectly reasonable 42% when it feels more like 77%. Enter the Si7021 Temperature + Humidity Sensor - the best way to prove the weatherman wrong! This lovely sensor for Silicon labs has ± 3% relative humidity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
  Adafruit Feather nRF52840: The Adafruit Feather nRF52840 Express is our take on an 'all-in-one' Arduino-compatible + Bluetooth Low Energy with built in USB plus battery charging, 1 MB of FLASH and 256KB of SRAM. With native USB it's even ready to join the CircuitPython party. For this chip, we've added Arduino IDE support - you can program the nRF52840 chip directly to take full advantage of the Cortex-M4 processor, and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
